# Fritzing sketch Arduino-Networking (saved by Fritzing 0.9.3b)

parts:
  Part1 = Arduino Ethernet Shield (Rev3)  # not connected
  U1 = ESP8266 WiFi Module [part_number=ESP8266]
  Part3 = Arduino Nano (Rev3.0)
  Part4 = Arduino Nano (Rev3.0)
  Part5 = ENC28J60 Breakout Board
  WeMos_D1_Mini1 = WeMos D1 Mini  # not connected
  M1 = DOIT Esp32 DevKit v1 (30 pins long, 11 pins width) [part_number=ESP32S-PIN30]  # not connected
  Part6 = Arduino Uno (Rev3)
  W5500_Module1 = W5500 Ethernet module [package="DIP (Dual Inline) [THT]"]
  Part7 = Arduino Nano (Rev3.0)
  U2 = ESP8266 WiFi Module [part_number=ESP8266]  # not connected
  R1 = Resistor [tolerance=±5% resistance=2k package=THT]
  R2 = Resistor [tolerance=±5% resistance=1k package=THT]
  R3 = Resistor [tolerance=±5% resistance=10k package=THT]

nets:
  N1: U1.RXD, R1.Pin_0, R2.Pin_0
  N2: U1.VCC, U1.GPIO_2, U1.CH_PD, R3.Pin_0
  GND: U1.GND, Part4.GND, Part4.RESET, R1.Pin_1
  N3: U1.TXD, Part4.D2
  N4: Part3.D8, Part3.D12/MISO, Part5.SO
  N5: Part3.D9, Part3.D10, Part5.CS
  N6: Part3.D11/MOSI, Part5.SI
  GND_2: Part3.VIN, Part3.GND, Part5.GND
  N7: Part3.RESET, Part5.RESET
  5V: Part3.5V, Part5.VCC
  N8: Part3.3V3, Part3.D13/SCK, Part5.SCK
  N9: Part4.D3, Part4.D4, R2.Pin_1
  N10: Part4.3V3, Part4.D13/SCK, R3.Pin_1
  N11: Part6.D10_PWM/SS, W5500_Module1.SCS
  N12: Part6.D11_PWM/MOSI, W5500_Module1.MOSI
  N13: Part6.D12/MISO, W5500_Module1.MISO
  N14: Part6.D13/SCK, W5500_Module1.SCLK
  N15: Part6.RESET, W5500_Module1.INT, W5500_Module1.RST
  5V_2: Part6.5V, W5500_Module1.5V
  GND_3: Part6.GND, W5500_Module1.GND
  N16: Part7.RESET, Part7.GND
  N17: Part7.5V, Part7.A7

notes:
  The ESP-01 operates at 3.3V whereas the Arduino is 5V. So, the Tx line from the Arduino needs to be stepped down using a voltage divider across two resistors:
  Arduino Pin 3 (or other assigned in code) - 1kΩ resistor - ESP-01 RX - 2kΩ resistor - GND
  Arduino Pin 2 (or other assigned in code) - ESP-01 TX
  Arduino 3.3V - 10kΩ resistor - ESP-01 VCC
  Arduino 3.3V - 10kΩ resistor - ESP-01 Enable
  Arduino GND - ESP-01 GND
  ESP-01 adaptor board provides power stepdown and logic level conversion enabling interface to the Arduino as follows:
  Arduino Pin 3 (or other assigned in code) - ESP-01 RX
  Arduino Pin 2 (or other assigned in code) - ESP-01 TX
  Arduino 5V - ESP-01 VCC
  Arduino GND - ESP-01 GND
  ENC28J60 chip operates at 3.3V, but it's data lines are 5V tolerant, so the following can be connected directly to Arduino SPI pins as follows:
  ENC28J60 CS - Arduino Pin 10
  ENC28J60 SI - Arduino Pin 11
  ENC28J60 SO - Arduino Pin 12
  ENC28J60 SCK - Arduino Pin 13
  ENC28J60 RESET - Arduino RST
  ENC28J60 GND - Arduino GND
  When it comes to the VCC power supply however, it's a bit more complicated.... some ENC28J60 breakout boards have onboard regulators that enable them to be supplied with 5V, while some require 3.3V (and some provide the option of either).
  If your ENC28J60 has a 5V input, you can connect the VCC pin directly to the 5V pin of the Arduino. BUT, if you have the 3.3V input, you can't just use the 3.3V pin instead - the ENC28J60 draws a lot of current - around 180mA when transferring data - which is more than the Arduino 3.3V regulator can supply. So, if you have the board that requires a 3.3V power supply, you'll need to use an external 3.3V power supply or stepdown from the 5V line instead.
  Arduino Ethernet shield uses SPI interface and slots ontop of an Arduino UNO, creating a connection to the necessary SPI pins - 10, 11, 12, and 13, as well as GND and 5V .
  When using a W5x00 in module form, use SPI connections to Arduino as follows:
  CS - Arduino Pin 10
  MOSI - Arduino Pin 11
  MISO - Arduino Pin 12
  CLK - Arduino Pin 13
  RESET - Arduino RST
  GND - Arduino GND
  VCC - Arduino 5V
  W5100 Ethernet Shield
  W5100/W5200/W5500 Module
  ENC28J60 Module
  ESP-01 with Adapter
  ESP-01
  ESP8266
  ESP32
  ESP8266 and ESP32 have built-in 802.11b/g/f/e Wi-Fi capability - no additional hardware required!
  Wired
  Wireless

custom parts:
  ESP8266 WiFi Module: Generic WiFi Module based on the ESP8266 with onboard PCB antenna and UART communications
  ENC28J60 Breakout Board: This is a breakout board for the Microchip ENC28J60 stand-alone ethernet controller. The ENC28J60 has an SPI interface. It operates at 3.3 Volts.
  WeMos D1 Mini: The D1 mini is a mini wifi board based on ESP-8266EX.
  DOIT Esp32 DevKit v1 (30 pins long, 11 pins width): The DOIT Esp32 DevKit v1 is one of the development board created by DOIT to evaluate the ESP-WROOM-32 module. It is based on the ESP32 microcontroller that boasts Wifi, Bluetooth, Ethernet and Low Power support all in a single chip. (vanepp) made breadboard work, adjusted pin numbering and labels and reduced size of schematic and cleaned up pcb. This chip is 30pins long (2 x15) and 11 pins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
  W5500 Ethernet module: W5500 based SPI Ethernet module for Arduino, etc.
